# Fritzing sketch DachaAlarm (saved by Fritzing 0.9.3b)

parts:
  Part1 = Arduino Uno (Rev3) - ICSP
  R1 = Resistor [tolerance=±5% resistance=10k package=THT]
  S1 = Reed switch [package=THT]

nets:
  N1: Part1.GND, R1.Pin_0
  N2: Part1.D4, R1.Pin_1, S1.pin_2
  N3: Part1.5V, S1.pin_1
